// Logisim project PC2.circ as structural Verilog: 8 circuits, main circuit main
module main (
);

  wire alu_uc_1_o0, alu_uc_1_o1, alu_uc_1_o2, alu_uc_1_o3, ALUSrc, and_1_out, and_2_out, and_3_out, BRANCH,
       button_1_out, button_2_out, clk, D0, D1, D2, D3, D4, D5, D6, Jump, LW, MEM_WRITE, MemRead, MemtoReg,
       OP0, OP1, REG_WRITE, REGDST, uc_1_alusrc, uc_1_branch, uc_1_memread, uc_1_memtoreg, uc_1_memwrite,
       uc_1_regdst, uc_1_regwrite, zero;
  wire [3:0] alu_uc_2_o0, bit_extender_6_out, bit_extender_6_out_2, bit_extender_7_out, bit_extender_7_out_2,
       bit_extender_8_out, bit_extender_8_out_2;
  wire [4:0] multiplexer_3_out, RS, RT;
  wire [5:0] FUNCT, OP;
  wire [15:6] Offset;
  wire [23:0] adder_1_out, bit_extender_1_out, bit_extender_2_out, bit_extender_9_out, C, multiplexer_1_out,
       PC;
  wire [25:0] DIRECCION;
  wire [31:0] alu_1_r, bit_extender_3_out, bit_extender_4_out, bit_extender_5_out, multiplexer_4_out,
       multiplexer_5_out, ram_1_data, ram_2_data, registro_1_data1, T, WRITE_DATA;

  ALU_UC alu_uc_1 (
    .ALUOp1(OP1), .ALUOp0(OP0), .F5(FUNCT[5]), .F4(FUNCT[4]), .F3(FUNCT[3]), .F2(FUNCT[2]), .F1(FUNCT[1]),
    .F0(FUNCT[0]), .O3(alu_uc_1_o3), .O2(alu_uc_1_o2), .O1(alu_uc_1_o1), .O0(alu_uc_1_o0));
  UC uc_1 (
    .OP5(OP[5]), .OP4(OP[4]), .RegDst(uc_1_regdst), .OP3(OP[3]), .OP2(OP[2]), .OP1(OP[1]), .OP0(OP[0]),
    .ALUSrc(uc_1_alusrc), .MemtoReg(uc_1_memtoreg), .RegWrite(uc_1_regwrite), .MemRead(uc_1_memread),
    .MemWrite(uc_1_memwrite), .Branch(uc_1_branch), .ALUOp1(OP1), .ALUOp0(OP0));  // open: Jump
  RAM #(.addrWidth(24), .dataWidth(32)) ram_1 (.addr(PC), .data(ram_1_data), .clr(button_1_out));  // open: sel, clk, ld
  Button button_1 (.out(button_1_out));
  OPCODE opcode_1 (
    .F5(FUNCT[5]), .F4(FUNCT[4]), .F3(FUNCT[3]), .F2(FUNCT[2]), .F1(FUNCT[1]), .F0(FUNCT[0]), .OP5(OP[5]),
    .OP4(OP[4]), .OP3(OP[3]), .OP2(OP[2]), .OP1(OP[1]), .OP0(OP[0]), .S0(D0), .S1(D1), .S2(D2), .S3(D3),
    .S4(D4), .S5(D5), .S6(D6));
  Adder #(.width(24)) adder_1 (.a(PC), .b(24'h1), .out(adder_1_out));  // open: cin, cout
  Bit_Extender #(.in_width(26), .out_width(24)) bit_extender_1 (.in(DIRECCION), .out(bit_extender_1_out));
  DECODE decode_1 (
    .in_1(ram_1_data), .FUNCT(FUNCT), .SHAMT(Offset[10:6]), .RD(Offset[15:11]), .RT(RT), .RS(RS), .OP(OP),
    .DIRECCION(DIRECCION));
  Multiplexer #(.width(24)) multiplexer_1 (
    .in0(adder_1_out), .in1(bit_extender_1_out), .out(multiplexer_1_out), .sel(Jump));  // open: en
  Register #(.width(24)) register_1 (.D(C), .Q(PC), .clk(clk), .clr(button_2_out));  // open: en
  Button button_2 (.out(button_2_out));
  _7_Segment_Display u_7_segment_display_1 (.g(D6), .f(D5), .a(D0), .b(D1), .e(D4), .d(D3), .c(D2));  // open: dp
  Multiplexer #(.width(24)) multiplexer_2 (
    .in0(multiplexer_1_out), .in1(bit_extender_2_out), .out(C), .sel(and_1_out));  // open: en
  assign bit_extender_2_out = {{8{1'b0}}, {Offset, FUNCT}};  // Bit_Extender bit_extender_2
  and and_1 (and_1_out, zero, BRANCH);
  assign bit_extender_3_out = {{6{1'b0}}, DIRECCION};  // Bit_Extender bit_extender_3
  Hex_Digit_Display hex_digit_display_1 (.value(bit_extender_3_out[27:24]));  // open: dp
  Hex_Digit_Display hex_digit_display_2 (.value(bit_extender_3_out[31:28]));  // open: dp
  Multiplexer #(.width(5)) multiplexer_3 (
    .in0(RT), .in1(Offset[15:11]), .out(multiplexer_3_out), .sel(REGDST));  // open: en
  UC uc_2 (
    .OP5(OP[5]), .OP4(OP[4]), .RegDst(REGDST), .OP3(OP[3]), .OP2(OP[2]), .OP1(OP[1]), .OP0(OP[0]),
    .ALUSrc(ALUSrc), .MemtoReg(MemtoReg), .RegWrite(REG_WRITE), .MemRead(MemRead), .MemWrite(MEM_WRITE),
    .Branch(BRANCH), .ALUOp1(OP1), .ALUOp0(OP0), .Jump(Jump));
  Hex_Digit_Display hex_digit_display_3 (.value(bit_extender_3_out[23:20]));  // open: dp
  Hex_Digit_Display hex_digit_display_4 (.value(bit_extender_3_out[19:16]));  // open: dp
  Clock clock_1 (.out(clk));
  assign bit_extender_4_out = {{27{1'b0}}, RS};  // Bit_Extender bit_extender_4
  REGISTRO registro_1 (
    .RS(RS), .WRITE_DATA(WRITE_DATA), .RT(RT), .REG_WRTIE(REG_WRITE), .data1(registro_1_data1), .data2(T),
    .WRITE_REGISTER(multiplexer_3_out), .clock(clk));
  assign bit_extender_5_out = {{16{1'b0}}, {Offset, FUNCT}};  // Bit_Extender bit_extender_5
  Hex_Digit_Display hex_digit_display_5 (.value(bit_extender_6_out_2));  // open: dp
  assign {bit_extender_6_out_2, bit_extender_6_out} = {{3{1'b0}}, RS};  // Bit_Extender bit_extender_6
  Hex_Digit_Display hex_digit_display_6 (.value(bit_extender_7_out_2));  // open: dp
  assign {bit_extender_7_out_2, bit_extender_7_out} = {{3{1'b0}}, RT};  // Bit_Extender bit_extender_7
  Hex_Digit_Display hex_digit_display_7 (.value(bit_extender_8_out_2));  // open: dp
  assign {bit_extender_8_out_2, bit_extender_8_out} = {{3{1'b0}}, Offset[15:11]};  // Bit_Extender bit_extender_8
  Hex_Digit_Display hex_digit_display_8 (.value(bit_extender_3_out[15:12]));  // open: dp
  Hex_Digit_Display hex_digit_display_9 (.value(bit_extender_3_out[11:8]));  // open: dp
  Multiplexer #(.width(32)) multiplexer_4 (
    .in0(registro_1_data1), .in1(bit_extender_4_out), .out(multiplexer_4_out), .sel(LW));  // open: en
  Multiplexer #(.width(32)) multiplexer_5 (
    .in0(T), .in1(bit_extender_5_out), .out(multiplexer_5_out), .sel(ALUSrc));  // open: en
  Hex_Digit_Display hex_digit_display_10 (.value(bit_extender_6_out));  // open: dp
  Hex_Digit_Display hex_digit_display_11 (.value(bit_extender_7_out));  // open: dp
  Hex_Digit_Display hex_digit_display_12 (.value(bit_extender_8_out));  // open: dp
  Hex_Digit_Display hex_digit_display_13 (.value(bit_extender_3_out[3:0]));  // open: dp
  Hex_Digit_Display hex_digit_display_14 (.value(bit_extender_3_out[7:4]));  // open: dp
  ALU alu_1 (
    .R(alu_1_r), .B(multiplexer_5_out), .A(multiplexer_4_out), .SELECT(alu_uc_2_o0), .zero(zero));  // open: CARRY_IN, CARRY_OUT
  ALU_UC alu_uc_2 (
    .ALUOp1(OP1), .ALUOp0(OP0), .F5(FUNCT[5]), .F4(FUNCT[4]), .F3(FUNCT[3]), .F2(FUNCT[2]), .F1(FUNCT[1]),
    .F0(FUNCT[0]), .O3(alu_uc_2_o0[3]), .O2(alu_uc_2_o0[2]), .O1(alu_uc_2_o0[1]), .O0(alu_uc_2_o0[0]));
  Bit_Extender #(.in_width(32), .out_width(24)) bit_extender_9 (.in(alu_1_r), .out(bit_extender_9_out));
  and and_2 (and_2_out, ALUSrc, MemtoReg, REG_WRITE, MemRead);
  and and_3 (and_3_out, MEM_WRITE, ALUSrc);
  or or_1 (LW, and_2_out, and_3_out);
  RAM #(.addrWidth(24), .dataWidth(32), .bus("separate")) ram_2 (
    .addr(bit_extender_9_out), .din(T), .data(ram_2_data), .str(MEM_WRITE), .clk(clk), .ld(MemRead));  // open: sel, clr
  Multiplexer #(.width(32)) multiplexer_6 (
    .in0(alu_1_r), .in1(ram_2_data), .out(WRITE_DATA), .sel(MemtoReg));  // open: en

  // Other names for the same wires on the sheet: Offset[5:0] = FUNCT; SHAMT[4:0] = Offset[10:6];
  //   RD[4:0] = Offset[15:11]

  // Notes on the sheet:
  //   A -> ADD
  //   S -> SUB
  //   n -> AND
  //   O -> OR
  //   E -> MULT
  //   b -> BEQ
  //   J -> J
  //   d -> ADDI
  //   L -> LW
  //   r -> SW
endmodule

module OPCODE (
  input  F5,
  input  F4,
  input  F3,
  input  F2,
  input  F1,
  input  F0,
  input  OP5,
  input  OP4,
  input  OP3,
  input  OP2,
  input  OP1,
  input  OP0,
  output S0,
  output S1,
  output S2,
  output S3,
  output S4,
  output S5,
  output S6
);

  wire and_1_out, and_2_out, and_3_out, and_4_out, and_5_out, and_6_out, and_7_out, and_8_out, and_9_out,
       and_10_out, and_11_out, and_12_out, and_13_out, and_14_out, and_15_out, and_16_out, and_17_out,
       and_18_out, and_19_out, and_20_out, and_21_out, and_22_out, and_23_out, and_24_out, and_25_out,
       and_26_out, and_27_out, and_28_out, and_29_out, and_30_out, and_31_out, and_32_out, and_33_out,
       and_34_out, and_35_out, and_36_out, not_1_out, not_2_out, not_3_out, not_4_out, not_5_out, not_6_out,
       not_7_out, not_8_out, not_9_out, not_10_out, not_11_out, not_12_out, not_13_out, not_14_out,
       not_15_out, not_16_out, not_17_out, not_18_out, not_19_out, not_20_out, not_21_out, not_22_out,
       not_23_out, not_24_out, not_25_out, not_26_out, not_27_out, not_28_out, not_29_out, not_30_out,
       not_31_out, not_32_out, not_33_out, not_34_out, not_35_out, not_36_out, not_37_out, not_38_out,
       not_39_out, not_40_out, not_41_out, not_42_out, not_43_out, not_44_out, not_45_out, not_46_out,
       not_47_out, not_48_out, not_49_out, not_50_out, not_51_out, not_52_out, not_53_out, not_54_out,
       not_55_out, not_56_out, not_57_out, not_58_out, not_59_out, not_60_out, not_61_out, not_62_out,
       not_63_out, not_64_out, not_65_out, not_66_out, not_67_out, not_68_out, not_69_out, not_70_out,
       not_71_out, not_72_out, not_73_out, not_74_out, not_75_out, not_76_out, not_77_out, not_78_out,
       not_79_out, not_80_out, not_81_out, not_82_out, not_83_out, not_84_out, not_85_out, not_86_out,
       not_87_out, not_88_out, not_89_out, not_90_out, not_91_out, not_92_out, not_93_out, not_94_out,
       not_95_out, not_96_out, not_97_out, not_98_out, not_99_out, not_100_out, not_101_out, not_102_out,
       not_103_out, not_104_out, not_105_out, not_106_out, not_107_out, not_108_out, not_109_out,
       not_110_out, not_111_out, not_112_out, not_113_out, not_114_out, not_115_out, not_116_out,
       not_117_out, not_118_out, not_119_out, not_120_out, not_121_out, not_122_out, not_123_out,
       not_124_out, not_125_out, not_126_out, not_127_out, not_128_out, not_129_out, not_130_out,
       not_131_out, not_132_out, not_133_out, not_134_out, not_135_out, not_136_out, not_137_out,
       not_138_out, not_139_out, not_140_out, not_141_out, not_142_out, not_143_out, not_144_out,
       not_145_out, not_146_out, not_147_out, not_148_out, not_149_out, not_150_out, not_151_out,
       not_152_out, not_153_out, not_154_out, not_155_out, not_156_out, not_157_out, not_158_out,
       not_159_out, not_160_out, not_161_out, not_162_out, not_163_out, not_164_out, not_165_out,
       not_166_out, not_167_out, not_168_out, not_169_out, not_170_out, not_171_out, not_172_out,
       not_173_out, not_174_out, not_175_out, not_176_out, not_177_out, not_178_out, not_179_out,
       not_180_out, not_181_out, not_182_out, not_183_out, not_184_out, not_185_out, not_186_out,
       not_187_out, not_188_out, not_189_out, not_190_out, not_191_out, not_192_out, not_193_out,
       not_194_out, not_195_out, not_196_out, not_197_out, not_198_out, not_199_out, not_200_out,
       not_201_out, not_202_out, not_203_out, not_204_out, not_205_out, not_206_out, not_207_out,
       not_208_out, not_209_out, not_210_out, not_211_out, not_212_out, not_213_out, not_214_out,
       not_215_out, not_216_out, not_217_out, not_218_out, not_219_out, not_220_out, not_221_out,
       not_222_out, not_223_out, not_224_out, not_225_out, not_226_out, not_227_out, not_228_out,
       not_229_out, not_230_out, not_231_out, not_232_out, not_233_out, not_234_out, not_235_out,
       not_236_out, not_237_out, not_238_out, not_239_out, not_240_out, not_241_out, not_242_out,
       not_243_out, not_244_out, not_245_out, not_246_out, not_247_out, not_248_out, not_249_out,
       not_250_out, not_251_out, not_252_out, not_253_out, not_254_out, not_255_out, not_256_out,
       not_257_out, not_258_out, not_259_out, not_260_out, not_261_out, not_262_out, not_263_out,
       not_264_out, not_265_out, not_266_out, not_267_out, not_268_out, not_269_out, not_270_out,
       not_271_out, not_272_out, not_273_out, not_274_out, not_275_out, not_276_out, not_277_out,
       not_278_out, not_279_out, not_280_out, not_281_out, not_282_out, not_283_out, not_284_out,
       not_285_out, not_286_out, not_287_out, not_288_out, not_289_out, not_290_out, not_291_out,
       not_292_out, not_293_out, not_294_out, not_295_out, not_296_out, not_297_out, not_298_out,
       not_299_out, not_300_out, not_301_out, not_302_out, not_303_out, not_304_out, not_305_out,
       not_306_out, not_307_out, not_308_out, not_309_out, not_310_out, not_311_out, not_312_out,
       not_313_out, not_314_out, not_315_out, not_316_out, not_317_out, not_318_out, not_319_out,
       not_320_out, not_321_out, not_322_out, not_323_out, not_324_out, not_325_out, not_326_out,
       not_327_out, not_328_out, not_329_out, not_330_out, not_331_out, not_332_out, not_333_out,
       not_334_out, not_335_out, not_336_out, not_337_out, not_338_out, not_339_out, not_340_out,
       not_341_out, not_342_out, not_343_out, not_344_out, not_345_out, not_346_out, not_347_out,
       not_348_out, not_349_out, not_350_out, not_351_out, not_352_out, not_353_out, not_354_out,
       not_355_out, not_356_out, not_357_out, not_358_out, not_359_out, not_360_out, not_361_out;

  not not_1 (not_1_out, F5);
  not not_2 (not_2_out, F4);
  not not_3 (not_3_out, F3);
  not not_4 (not_4_out, F2);
  not not_5 (not_5_out, F1);
  not not_6 (not_6_out, F0);
  not not_7 (not_7_out, OP4);
  not not_8 (not_8_out, OP2);
  not not_9 (not_9_out, F5);
  not not_10 (not_10_out, F2);
  not not_11 (not_11_out, F1);
  not not_12 (not_12_out, F0);
  not not_13 (not_13_out, OP5);
  not not_14 (not_14_out, OP4);
  not not_15 (not_15_out, OP3);
  not not_16 (not_16_out, OP2);
  not not_17 (not_17_out, OP1);
  not not_18 (not_18_out, OP0);
  not not_19 (not_19_out, F4);
  not not_20 (not_20_out, F3);
  not not_21 (not_21_out, F2);
  not not_22 (not_22_out, F0);
  not not_23 (not_23_out, OP5);
  not not_24 (not_24_out, OP4);
  not not_25 (not_25_out, OP3);
  not not_26 (not_26_out, OP2);
  not not_27 (not_27_out, OP1);
  not not_28 (not_28_out, OP0);
  not not_29 (not_29_out, F4);
  not not_30 (not_30_out, F3);
  not not_31 (not_31_out, F1);
  not not_32 (not_32_out, OP5);
  not not_33 (not_33_out, OP4);
  not not_34 (not_34_out, OP3);
  not not_35 (not_35_out, OP2);
  not not_36 (not_36_out, OP1);
  not not_37 (not_37_out, OP0);
  not not_38 (not_38_out, F5);
  not not_39 (not_39_out, F4);
  not not_40 (not_40_out, F3);
  not not_41 (not_41_out, F2);
  not not_42 (not_42_out, F1);
  not not_43 (not_43_out, F0);
  not not_44 (not_44_out, OP5);
  not not_45 (not_45_out, OP4);
  not not_46 (not_46_out, OP3);
  not not_47 (not_47_out, OP2);
  not not_48 (not_48_out, OP0);
  not not_49 (not_49_out, F5);
  not not_50 (not_50_out, F4);
  not not_51 (not_51_out, F3);
  not not_52 (not_52_out, F2);
  not not_53 (not_53_out, F1);
  not not_54 (not_54_out, F0);
  not not_55 (not_55_out, OP5);
  not not_56 (not_56_out, OP4);
  not not_57 (not_57_out, OP2);
  not not_58 (not_58_out, OP1);
  not not_59 (not_59_out, OP0);
  not not_60 (not_60_out, F4);
  not not_61 (not_61_out, F3);
  not not_62 (not_62_out, F1);
  not not_63 (not_63_out, F0);
  not not_64 (not_64_out, OP5);
  not not_65 (not_65_out, OP4);
  not not_66 (not_66_out, OP3);
  not not_67 (not_67_out, OP2);
  not not_68 (not_68_out, OP1);
  not not_69 (not_69_out, OP0);
  not not_70 (not_70_out, F4);
  not not_71 (not_71_out, F3);
  not not_72 (not_72_out, F1);
  not not_73 (not_73_out, OP5);
  not not_74 (not_74_out, OP4);
  not not_75 (not_75_out, OP3);
  not not_76 (not_76_out, OP2);
  not not_77 (not_77_out, OP1);
  not not_78 (not_78_out, OP0);
  not not_79 (not_79_out, F5);
  not not_80 (not_80_out, F4);
  not not_81 (not_81_out, F3);
  not not_82 (not_82_out, F2);
  not not_83 (not_83_out, F1);
  not not_84 (not_84_out, F0);
  not not_85 (not_85_out, OP5);
  not not_86 (not_86_out, OP4);
  not not_87 (not_87_out, OP3);
  not not_88 (not_88_out, OP2);
  not not_89 (not_89_out, OP0);
  not not_90 (not_90_out, F5);
  not not_91 (not_91_out, F4);
  not not_92 (not_92_out, F3);
  not not_93 (not_93_out, F2);
  not not_94 (not_94_out, F1);
  not not_95 (not_95_out, F0);
  not not_96 (not_96_out, OP5);
  not not_97 (not_97_out, OP4);
  not not_98 (not_98_out, OP3);
  not not_99 (not_99_out, OP1);
  not not_100 (not_100_out, OP0);
  not not_101 (not_101_out, F5);
  not not_102 (not_102_out, F4);
  not not_103 (not_103_out, F3);
  not not_104 (not_104_out, F2);
  not not_105 (not_105_out, F1);
  not not_106 (not_106_out, F0);
  not not_107 (not_107_out, OP5);
  not not_108 (not_108_out, OP4);
  not not_109 (not_109_out, OP2);
  not not_110 (not_110_out, OP1);
  not not_111 (not_111_out, OP0);
  not not_112 (not_112_out, F4);
  not not_113 (not_113_out, F3);
  not not_114 (not_114_out, F2);
  not not_115 (not_115_out, F0);
  not not_116 (not_116_out, OP5);
  not not_117 (not_117_out, OP4);
  not not_118 (not_118_out, OP3);
  not not_119 (not_119_out, OP2);
  not not_120 (not_120_out, OP1);
  not not_121 (not_121_out, OP0);
  not not_122 (not_122_out, F4);
  not not_123 (not_123_out, F3);
  not not_124 (not_124_out, F1);
  not not_125 (not_125_out, OP5);
  not not_126 (not_126_out, OP4);
  not not_127 (not_127_out, OP3);
  not not_128 (not_128_out, OP2);
  not not_129 (not_129_out, OP1);
  not not_130 (not_130_out, OP0);
  not not_131 (not_131_out, F5);
  not not_132 (not_132_out, F4);
  not not_133 (not_133_out, F3);
  not not_134 (not_134_out, F2);
  not not_135 (not_135_out, F1);
  not not_136 (not_136_out, F0);
  not not_137 (not_137_out, OP5);
  not not_138 (not_138_out, OP4);
  not not_139 (not_139_out, OP3);
  not not_140 (not_140_out, OP2);
  not not_141 (not_141_out, OP0);
  not not_142 (not_142_out, F5);
  not not_143 (not_143_out, F4);
  not not_144 (not_144_out, F3);
  not not_145 (not_145_out, F2);
  not not_146 (not_146_out, F1);
  not not_147 (not_147_out, F0);
  not not_148 (not_148_out, OP5);
  not not_149 (not_149_out, OP4);
  not not_150 (not_150_out, OP3);
  not not_151 (not_151_out, OP1);
  not not_152 (not_152_out, OP0);
  not not_153 (not_153_out, F5);
  not not_154 (not_154_out, F4);
  not not_155 (not_155_out, F3);
  not not_156 (not_156_out, F2);
  not not_157 (not_157_out, F1);
  not not_158 (not_158_out, F0);
  not not_159 (not_159_out, OP5);
  not not_160 (not_160_out, OP4);
  not not_161 (not_161_out, OP2);
  not not_162 (not_162_out, OP1);
  not not_163 (not_163_out, OP0);
  not not_164 (not_164_out, F5);
  not not_165 (not_165_out, F4);
  not not_166 (not_166_out, F3);
  not not_167 (not_167_out, F2);
  not not_168 (not_168_out, F1);
  not not_169 (not_169_out, F0);
  not not_170 (not_170_out, OP4);
  not not_171 (not_171_out, OP3);
  not not_172 (not_172_out, OP2);
  not not_173 (not_173_out, F5);
  not not_174 (not_174_out, F2);
  not not_175 (not_175_out, F1);
  not not_176 (not_176_out, F0);
  not not_177 (not_177_out, OP5);
  not not_178 (not_178_out, OP4);
  not not_179 (not_179_out, OP3);
  not not_180 (not_180_out, OP2);
  not not_181 (not_181_out, OP1);
  not not_182 (not_182_out, OP0);
  not not_183 (not_183_out, F4);
  not not_184 (not_184_out, F3);
  not not_185 (not_185_out, F2);
  not not_186 (not_186_out, F0);
  not not_187 (not_187_out, OP5);
  not not_188 (not_188_out, OP4);
  not not_189 (not_189_out, OP3);
  not not_190 (not_190_out, OP2);
  not not_191 (not_191_out, OP1);
  not not_192 (not_192_out, OP0);
  not not_193 (not_193_out, F4);
  not not_194 (not_194_out, F3);
  not not_195 (not_195_out, F1);
  not not_196 (not_196_out, OP5);
  not not_197 (not_197_out, OP4);
  not not_198 (not_198_out, OP3);
  not not_199 (not_199_out, OP2);
  not not_200 (not_200_out, OP1);
  not not_201 (not_201_out, OP0);
  not not_202 (not_202_out, F5);
  not not_203 (not_203_out, F4);
  not not_204 (not_204_out, F3);
  not not_205 (not_205_out, F2);
  not not_206 (not_206_out, F1);
  not not_207 (not_207_out, F0);
  not not_208 (not_208_out, OP5);
  not not_209 (not_209_out, OP4);
  not not_210 (not_210_out, OP3);
  not not_211 (not_211_out, OP2);
  not not_212 (not_212_out, OP0);
  not not_213 (not_213_out, F5);
  not not_214 (not_214_out, F4);
  not not_215 (not_215_out, F3);
  not not_216 (not_216_out, F2);
  not not_217 (not_217_out, F1);
  not not_218 (not_218_out, F0);
  not not_219 (not_219_out, OP5);
  not not_220 (not_220_out, OP4);
  not not_221 (not_221_out, OP3);
  not not_222 (not_222_out, OP1);
  not not_223 (not_223_out, OP0);
  not not_224 (not_224_out, F5);
  not not_225 (not_225_out, F4);
  not not_226 (not_226_out, F3);
  not not_227 (not_227_out, F2);
  not not_228 (not_228_out, F1);
  not not_229 (not_229_out, F0);
  not not_230 (not_230_out, OP5);
  not not_231 (not_231_out, OP4);
  not not_232 (not_232_out, OP2);
  not not_233 (not_233_out, OP1);
  not not_234 (not_234_out, OP0);
  not not_235 (not_235_out, F5);
  not not_236 (not_236_out, F4);
  not not_237 (not_237_out, F3);
  not not_238 (not_238_out, F2);
  not not_239 (not_239_out, F1);
  not not_240 (not_240_out, F0);
  not not_241 (not_241_out, OP4);
  not not_242 (not_242_out, OP2);
  not not_243 (not_243_out, F5);
  not not_244 (not_244_out, F2);
  not not_245 (not_245_out, F1);
  not not_246 (not_246_out, F0);
  not not_247 (not_247_out, OP5);
  not not_248 (not_248_out, OP4);
  not not_249 (not_249_out, OP3);
  not not_250 (not_250_out, OP2);
  not not_251 (not_251_out, OP1);
  not not_252 (not_252_out, OP0);
  not not_253 (not_253_out, F4);
  not not_254 (not_254_out, F3);
  not not_255 (not_255_out, F1);
  not not_256 (not_256_out, F0);
  not not_257 (not_257_out, OP5);
  not not_258 (not_258_out, OP4);
  not not_259 (not_259_out, OP3);
  not not_260 (not_260_out, OP2);
  not not_261 (not_261_out, OP1);
  not not_262 (not_262_out, OP0);
  not not_263 (not_263_out, F4);
  not not_264 (not_264_out, F3);
  not not_265 (not_265_out, F1);
  not not_266 (not_266_out, OP5);
  not not_267 (not_267_out, OP4);
  not not_268 (not_268_out, OP3);
  not not_269 (not_269_out, OP2);
  not not_270 (not_270_out, OP1);
  not not_271 (not_271_out, OP0);
  not not_272 (not_272_out, F5);
  not not_273 (not_273_out, F4);
  not not_274 (not_274_out, F3);
  not not_275 (not_275_out, F2);
  not not_276 (not_276_out, F1);
  not not_277 (not_277_out, F0);
  not not_278 (not_278_out, OP5);
  not not_279 (not_279_out, OP4);
  not not_280 (not_280_out, OP3);
  not not_281 (not_281_out, OP1);
  not not_282 (not_282_out, OP0);
  not not_283 (not_283_out, F5);
  not not_284 (not_284_out, F4);
  not not_285 (not_285_out, F3);
  not not_286 (not_286_out, F2);
  not not_287 (not_287_out, F1);
  not not_288 (not_288_out, F0);
  not not_289 (not_289_out, OP4);
  not not_290 (not_290_out, OP2);
  not not_291 (not_291_out, F5);
  not not_292 (not_292_out, F2);
  not not_293 (not_293_out, F1);
  not not_294 (not_294_out, F0);
  not not_295 (not_295_out, OP5);
  not not_296 (not_296_out, OP4);
  not not_297 (not_297_out, OP3);
  not not_298 (not_298_out, OP2);
  not not_299 (not_299_out, OP1);
  not not_300 (not_300_out, OP0);
  not not_301 (not_301_out, F4);
  not not_302 (not_302_out, F3);
  not not_303 (not_303_out, F2);
  not not_304 (not_304_out, F0);
  not not_305 (not_305_out, OP5);
  not not_306 (not_306_out, OP4);
  not not_307 (not_307_out, OP3);
  not not_308 (not_308_out, OP2);
  not not_309 (not_309_out, OP1);
  not not_310 (not_310_out, OP0);
  not not_311 (not_311_out, F4);
  not not_312 (not_312_out, F3);
  not not_313 (not_313_out, F1);
  not not_314 (not_314_out, OP5);
  not not_315 (not_315_out, OP4);
  not not_316 (not_316_out, OP3);
  not not_317 (not_317_out, OP2);
  not not_318 (not_318_out, OP1);
  not not_319 (not_319_out, OP0);
  not not_320 (not_320_out, F5);
  not not_321 (not_321_out, F4);
  not not_322 (not_322_out, F3);
  not not_323 (not_323_out, F2);
  not not_324 (not_324_out, F1);
  not not_325 (not_325_out, F0);
  not not_326 (not_326_out, OP5);
  not not_327 (not_327_out, OP4);
  not not_328 (not_328_out, OP3);
  not not_329 (not_329_out, OP1);
  not not_330 (not_330_out, OP0);
  not not_331 (not_331_out, F5);
  not not_332 (not_332_out, F4);
  not not_333 (not_333_out, F3);
  not not_334 (not_334_out, F2);
  not not_335 (not_335_out, F1);
  not not_336 (not_336_out, F0);
  not not_337 (not_337_out, OP5);
  not not_338 (not_338_out, OP4);
  not not_339 (not_339_out, OP2);
  not not_340 (not_340_out, OP1);
  not not_341 (not_341_out, OP0);
  not not_342 (not_342_out, F5);
  not not_343 (not_343_out, F2);
  not not_344 (not_344_out, F1);
  not not_345 (not_345_out, F0);
  not not_346 (not_346_out, OP5);
  not not_347 (not_347_out, OP4);
  not not_348 (not_348_out, OP3);
  not not_349 (not_349_out, OP2);
  not not_350 (not_350_out, OP1);
  not not_351 (not_351_out, OP0);
  not not_352 (not_352_out, F4);
  not not_353 (not_353_out, F3);
  not not_354 (not_354_out, F2);
  not not_355 (not_355_out, F0);
  not not_356 (not_356_out, OP5);
  not not_357 (not_357_out, OP4);
  not not_358 (not_358_out, OP3);
  not not_359 (not_359_out, OP2);
  not not_360 (not_360_out, OP1);
  not not_361 (not_361_out, OP0);
  and and_1 (and_1_out, not_1_out, not_2_out, not_3_out, not_4_out, not_5_out, not_6_out, OP5, not_7_out, OP3, not_8_out, OP1, OP0);
  and and_2 (and_2_out, not_9_out, F4, F3, not_10_out, not_11_out, not_12_out, not_13_out, not_14_out, not_15_out, not_16_out, not_17_out, not_18_out);
  and and_3 (and_3_out, F5, not_19_out, not_20_out, not_21_out, not_22_out, not_23_out, not_24_out, not_25_out, not_26_out, not_27_out, not_28_out);
  and and_4 (and_4_out, F5, not_29_out, not_30_out, F2, not_31_out, not_32_out, not_33_out, not_34_out, not_35_out, not_36_out, not_37_out);
  and and_5 (and_5_out, not_38_out, not_39_out, not_40_out, not_41_out, not_42_out, not_43_out, not_44_out, not_45_out, not_46_out, not_47_out, OP1, not_48_out);
  and and_6 (and_6_out, not_49_out, not_50_out, not_51_out, not_52_out, not_53_out, not_54_out, not_55_out, not_56_out, OP3, not_57_out, not_58_out, not_59_out);
  and and_7 (and_7_out, F5, not_60_out, not_61_out, not_62_out, not_63_out, not_64_out, not_65_out, not_66_out, not_67_out, not_68_out, not_69_out);
  and and_8 (and_8_out, F5, not_70_out, not_71_out, F2, not_72_out, not_73_out, not_74_out, not_75_out, not_76_out, not_77_out, not_78_out);
  and and_9 (and_9_out, not_79_out, not_80_out, not_81_out, not_82_out, not_83_out, not_84_out, not_85_out, not_86_out, not_87_out, not_88_out, OP1, not_89_out);
  and and_10 (and_10_out, not_90_out, not_91_out, not_92_out, not_93_out, not_94_out, not_95_out, not_96_out, not_97_out, not_98_out, OP2, not_99_out, not_100_out);
  and and_11 (and_11_out, not_101_out, not_102_out, not_103_out, not_104_out, not_105_out, not_106_out, not_107_out, not_108_out, OP3, not_109_out, not_110_out, not_111_out);
  and and_12 (and_12_out, F5, not_112_out, not_113_out, not_114_out, not_115_out, not_116_out, not_117_out, not_118_out, not_119_out, not_120_out, not_121_out);
  and and_13 (and_13_out, F5, not_122_out, not_123_out, F2, not_124_out, not_125_out, not_126_out, not_127_out, not_128_out, not_129_out, not_130_out);
  and and_14 (and_14_out, not_131_out, not_132_out, not_133_out, not_134_out, not_135_out, not_136_out, not_137_out, not_138_out, not_139_out, not_140_out, OP1, not_141_out);
  and and_15 (and_15_out, not_142_out, not_143_out, not_144_out, not_145_out, not_146_out, not_147_out, not_148_out, not_149_out, not_150_out, OP2, not_151_out, not_152_out);
  and and_16 (and_16_out, not_153_out, not_154_out, not_155_out, not_156_out, not_157_out, not_158_out, not_159_out, not_160_out, OP3, not_161_out, not_162_out, not_163_out);
  and and_17 (and_17_out, not_164_out, not_165_out, not_166_out, not_167_out, not_168_out, not_169_out, OP5, not_170_out, not_171_out, not_172_out, OP1, OP0);
  and and_18 (and_18_out, not_173_out, F4, F3, not_174_out, not_175_out, not_176_out, not_177_out, not_178_out, not_179_out, not_180_out, not_181_out, not_182_out);
  and and_19 (and_19_out, F5, not_183_out, not_184_out, not_185_out, F1, not_186_out, not_187_out, not_188_out, not_189_out, not_190_out, not_191_out, not_192_out);
  and and_20 (and_20_out, F5, not_193_out, not_194_out, F2, not_195_out, F0, not_196_out, not_197_out, not_198_out, not_199_out, not_200_out, not_201_out);
  and and_21 (and_21_out, not_202_out, not_203_out, not_204_out, not_205_out, not_206_out, not_207_out, not_208_out, not_209_out, not_210_out, not_211_out, OP1, not_212_out);
  and and_22 (and_22_out, not_213_out, not_214_out, not_215_out, not_216_out, not_217_out, not_218_out, not_219_out, not_220_out, not_221_out, OP2, not_222_out, not_223_out);
  and and_23 (and_23_out, not_224_out, not_225_out, not_226_out, not_227_out, not_228_out, not_229_out, not_230_out, not_231_out, OP3, not_232_out, not_233_out, not_234_out);
  and and_24 (and_24_out, not_235_out, not_236_out, not_237_out, not_238_out, not_239_out, not_240_out, OP5, not_241_out, not_242_out, OP1, OP0);
  and and_25 (and_25_out, not_243_out, F4, F3, not_244_out, not_245_out, not_246_out, not_247_out, not_248_out, not_249_out, not_250_out, not_251_out, not_252_out);
  and and_26 (and_26_out, F5, not_253_out, not_254_out, not_255_out, not_256_out, not_257_out, not_258_out, not_259_out, not_260_out, not_261_out, not_262_out);
  and and_27 (and_27_out, F5, not_263_out, not_264_out, F2, not_265_out, not_266_out, not_267_out, not_268_out, not_269_out, not_270_out, not_271_out);
  and and_28 (and_28_out, not_272_out, not_273_out, not_274_out, not_275_out, not_276_out, not_277_out, not_278_out, not_279_out, not_280_out, OP2, not_281_out, not_282_out);
  and and_29 (and_29_out, not_283_out, not_284_out, not_285_out, not_286_out, not_287_out, not_288_out, OP5, not_289_out, not_290_out, OP1, OP0);
  and and_30 (and_30_out, not_291_out, F4, F3, not_292_out, not_293_out, not_294_out, not_295_out, not_296_out, not_297_out, not_298_out, not_299_out, not_300_out);
  and and_31 (and_31_out, F5, not_301_out, not_302_out, not_303_out, not_304_out, not_305_out, not_306_out, not_307_out, not_308_out, not_309_out, not_310_out);
  and and_32 (and_32_out, F5, not_311_out, not_312_out, F2, not_313_out, not_314_out, not_315_out, not_316_out, not_317_out, not_318_out, not_319_out);
  and and_33 (and_33_out, not_320_out, not_321_out, not_322_out, not_323_out, not_324_out, not_325_out, not_326_out, not_327_out, not_328_out, OP2, not_329_out, not_330_out);
  and and_34 (and_34_out, not_331_out, not_332_out, not_333_out, not_334_out, not_335_out, not_336_out, not_337_out, not_338_out, OP3, not_339_out, not_340_out, not_341_out);
  and and_35 (and_35_out, not_342_out, F4, F3, not_343_out, not_344_out, not_345_out, not_346_out, not_347_out, not_348_out, not_349_out, not_350_out, not_351_out);
  and and_36 (and_36_out, F5, not_352_out, not_353_out, not_354_out, not_355_out, not_356_out, not_357_out, not_358_out, not_359_out, not_360_out, not_361_out);
  or or_1 (S0, and_1_out, and_2_out, and_3_out, and_4_out);
  or or_2 (S1, and_5_out, and_6_out, and_7_out, and_8_out);
  or or_3 (S2, and_9_out, and_10_out, and_11_out, and_12_out, and_13_out);
  or or_4 (S3, and_14_out, and_15_out, and_16_out, and_17_out, and_18_out, and_19_out, and_20_out);
  or or_5 (S4, and_21_out, and_22_out, and_23_out, and_24_out, and_25_out, and_26_out, and_27_out);
  or or_6 (S5, and_28_out, and_29_out, and_30_out, and_31_out, and_32_out);
  or or_7 (S6, and_33_out, and_34_out, and_35_out, and_36_out);
endmodule

module DECODE (
  input  [31:0] in_1,
  output [5:0] FUNCT,
  output [4:0] SHAMT,
  output [4:0] RD,
  output [4:0] RT,
  output [4:0] RS,
  output [5:0] OP,
  output [25:0] DIRECCION
);


  assign DIRECCION = in_1[25:0];
  assign FUNCT = in_1[5:0];
  assign OP = in_1[31:26];
  assign RD = in_1[15:11];
  assign RS = in_1[25:21];
  assign RT = in_1[20:16];
  assign SHAMT = in_1[10:6];
endmodule

module DEBUGGING (
  input  E0,
  input  E1,
  input  E2,
  input  E3,
  output S0,
  output S1,
  output S2,
  output S3,
  output S4,
  output S5,
  output S6
);

  wire and_1_out, and_2_out, and_3_out, and_4_out, and_5_out, and_6_out, and_7_out, and_8_out, and_9_out,
       and_10_out, and_11_out, and_12_out, and_13_out, and_14_out, and_15_out, and_16_out, and_17_out,
       and_18_out, and_19_out, and_20_out, and_21_out, and_22_out, and_23_out, and_24_out, and_25_out,
       and_26_out, and_27_out, and_28_out, and_29_out, and_30_out, and_31_out, and_32_out, and_33_out,
       not_1_out, not_2_out, not_3_out, not_4_out, not_5_out, not_6_out, not_7_out, not_8_out, not_9_out,
       not_10_out, not_11_out, not_12_out, not_13_out, not_14_out, not_15_out, not_16_out, not_17_out,
       not_18_out, not_19_out, not_20_out, not_21_out, not_22_out, not_23_out, not_24_out, not_25_out,
       not_26_out, not_27_out, not_28_out, not_29_out, not_30_out, not_31_out, not_32_out, not_33_out,
       not_34_out, not_35_out, not_36_out, not_37_out, not_38_out, not_39_out, not_40_out, not_41_out;

  not not_1 (not_1_out, E1);
  and and_1 (and_1_out, not_1_out, not_2_out);
  not not_2 (not_2_out, E3);
  not not_3 (not_3_out, E0);
  and and_2 (and_2_out, not_3_out, E2);
  not not_4 (not_4_out, E0);
  and and_3 (and_3_out, not_4_out, E1, E3);
  and and_4 (and_4_out, E1, E2);
  and and_5 (and_5_out, E0, not_5_out, not_6_out);
  not not_5 (not_5_out, E1);
  not not_6 (not_6_out, E2);
  and and_6 (and_6_out, E0, not_7_out);
  not not_7 (not_7_out, E3);
  not not_8 (not_8_out, E0);
  and and_7 (and_7_out, not_8_out, not_9_out);
  not not_9 (not_9_out, E1);
  not not_10 (not_10_out, E0);
  and and_8 (and_8_out, not_10_out, not_11_out, not_12_out);
  not not_11 (not_11_out, E2);
  not not_12 (not_12_out, E3);
  not not_13 (not_13_out, E1);
  and and_9 (and_9_out, not_13_out, not_14_out);
  not not_14 (not_14_out, E3);
  not not_15 (not_15_out, E0);
  and and_10 (and_10_out, not_15_out, E2, E3);
  not not_16 (not_16_out, E2);
  and and_11 (and_11_out, E0, not_16_out, E3);
  not not_17 (not_17_out, E0);
  and and_12 (and_12_out, not_17_out, not_18_out);
  not not_18 (not_18_out, E2);
  not not_19 (not_19_out, E0);
  and and_13 (and_13_out, not_19_out, E3);
  not not_20 (not_20_out, E2);
  and and_14 (and_14_out, not_20_out, E3);
  not not_21 (not_21_out, E0);
  and and_15 (and_15_out, not_21_out, E1);
  and and_16 (and_16_out, E0, not_22_out);
  not not_22 (not_22_out, E1);
  not not_23 (not_23_out, E0);
  not not_24 (not_24_out, E1);
  and and_17 (and_17_out, not_23_out, not_24_out, not_25_out);
  not not_25 (not_25_out, E3);
  not not_26 (not_26_out, E1);
  and and_18 (and_18_out, not_26_out, E2, E3);
  and and_19 (and_19_out, E1, not_27_out, E3);
  not not_27 (not_27_out, E2);
  and and_20 (and_20_out, E1, E2, not_28_out);
  not not_28 (not_28_out, E3);
  not not_29 (not_29_out, E2);
  and and_21 (and_21_out, E0, not_29_out, not_30_out);
  not not_30 (not_30_out, E3);
  not not_31 (not_31_out, E1);
  and and_22 (and_22_out, not_31_out, not_32_out);
  not not_32 (not_32_out, E3);
  and and_23 (and_23_out, E2, not_33_out);
  not not_33 (not_33_out, E3);
  and and_24 (and_24_out, E0, E2);
  and and_25 (and_25_out, E0, E1);
  not not_34 (not_34_out, E2);
  and and_26 (and_26_out, not_34_out, not_35_out);
  not not_35 (not_35_out, E3);
  not not_36 (not_36_out, E0);
  and and_27 (and_27_out, not_36_out, E1, not_37_out);
  not not_37 (not_37_out, E2);
  and and_28 (and_28_out, E1, not_38_out);
  not not_38 (not_38_out, E3);
  and and_29 (and_29_out, E0, not_39_out);
  not not_39 (not_39_out, E1);
  and and_30 (and_30_out, E0, E2);
  not not_40 (not_40_out, E0);
  and and_31 (and_31_out, not_40_out, E1);
  and and_32 (and_32_out, E1, E3);
  and and_33 (and_33_out, E0, not_41_out);
  not not_41 (not_41_out, E1);
  or or_1 (S1, and_7_out, and_8_out, and_9_out, and_10_out, and_11_out);
  or or_2 (S2, and_12_out, and_13_out, and_14_out, and_15_out, and_16_out);
  or or_3 (S3, and_17_out, and_18_out, and_19_out, and_20_out, and_21_out);
  or or_4 (S4, and_22_out, and_23_out, and_24_out, and_25_out);
  or or_5 (S5, and_26_out, and_27_out, and_28_out, and_29_out, and_30_out);
  or or_6 (S6, E2, and_31_out, and_32_out, and_33_out);
  or or_7 (S0, and_1_out, and_2_out, and_3_out, and_4_out, and_5_out, and_6_out);
endmodule

// registro
module REGISTRO (
  input  clock,
  input  [4:0] RS,
  input  [31:0] WRITE_DATA,
  input  [4:0] RT,
  input  REG_WRTIE,
  input  [4:0] WRITE_REGISTER,
  output [31:0] data1,
  output [31:0] data2
);

  wire E0, E1, E2, E3, E4, E5, E6, E7, E8, E9, E10, E11, E12, E13, E14, E15, E16, E17, E18, E19, E20, E21,
       E22, E23, E24, E25, E26, E27, E28, E29, E30, E31;
  wire [31:0] R0, R1, R2, R3, R4, R5, R6, R7, R8, R9, R10, R11, R12, R13, R14, R15, R16, R17, R18, R19, R20,
       R21, R22, R23, R24, R25, R26, R27, R28, R29, R30, R31;

  Register #(.width(32)) register_1 (.D(WRITE_DATA), .en(E0), .Q(R0), .clk(clock));  // open: clr
  Register #(.width(32)) register_2 (.D(WRITE_DATA), .en(E4), .Q(R4), .clk(clock));  // open: clr
  Register #(.width(32)) register_3 (.D(WRITE_DATA), .en(E8), .Q(R8), .clk(clock));  // open: clr
  Register #(.width(32)) register_4 (.D(WRITE_DATA), .en(E12), .Q(R12), .clk(clock));  // open: clr
  Register #(.width(32)) register_5 (.D(WRITE_DATA), .en(E16), .Q(R16), .clk(clock));  // open: clr
  Register #(.width(32)) register_6 (.D(WRITE_DATA), .en(E20), .Q(R20), .clk(clock));  // open: clr
  Register #(.width(32)) register_7 (.D(WRITE_DATA), .en(E24), .Q(R24), .clk(clock));  // open: clr
  Register #(.width(32)) register_8 (.D(WRITE_DATA), .en(E28), .Q(R28), .clk(clock));  // open: clr
  Register #(.width(32)) register_9 (.D(WRITE_DATA), .en(E1), .Q(R1), .clk(clock));  // open: clr
  Register #(.width(32)) register_10 (.D(WRITE_DATA), .en(E5), .Q(R5), .clk(clock));  // open: clr
  Register #(.width(32)) register_11 (.D(WRITE_DATA), .en(E9), .Q(R9), .clk(clock));  // open: clr
  Register #(.width(32)) register_12 (.D(WRITE_DATA), .en(E13), .Q(R13), .clk(clock));  // open: clr
  Register #(.width(32)) register_13 (.D(WRITE_DATA), .en(E17), .Q(R17), .clk(clock));  // open: clr
  Register #(.width(32)) register_14 (.D(WRITE_DATA), .en(E21), .Q(R21), .clk(clock));  // open: clr
  Register #(.width(32)) register_15 (.D(WRITE_DATA), .en(E25), .Q(R25), .clk(clock));  // open: clr
  Register #(.width(32)) register_16 (.D(WRITE_DATA), .en(E29), .Q(R29), .clk(clock));  // open: clr
  Demultiplexer #(.select(5)) demultiplexer_1 (
    .out0(E0), .out1(E1), .out2(E2), .out3(E3), .out4(E4), .out5(E5), .out6(E6), .out7(E7), .out8(E8),
    .out9(E9), .out10(E10), .out11(E11), .out12(E12), .out13(E13), .out14(E14), .out15(E15), .out16(E16),
    .out17(E17), .out18(E18), .out19(E19), .out20(E20), .out21(E21), .out22(E22), .out23(E23), .out24(E24),
    .out25(E25), .out26(E26), .out27(E27), .out28(E28), .out29(E29), .out30(E30), .out31(E31),
    .in(REG_WRTIE), .sel(WRITE_REGISTER));  // open: en
  Register #(.width(32)) register_17 (.D(WRITE_DATA), .en(E2), .Q(R2), .clk(clock));  // open: clr
  Register #(.width(32)) register_18 (.D(WRITE_DATA), .en(E6), .Q(R6), .clk(clock));  // open: clr
  Register #(.width(32)) register_19 (.D(WRITE_DATA), .en(E10), .Q(R10), .clk(clock));  // open: clr
  Register #(.width(32)) register_20 (.D(WRITE_DATA), .en(E14), .Q(R14), .clk(clock));  // open: clr
  Register #(.width(32)) register_21 (.D(WRITE_DATA), .en(E18), .Q(R18), .clk(clock));  // open: clr
  Register #(.width(32)) register_22 (.D(WRITE_DATA), .en(E22), .Q(R22), .clk(clock));  // open: clr
  Register #(.width(32)) register_23 (.D(WRITE_DATA), .en(E26), .Q(R26), .clk(clock));  // open: clr
  Register #(.width(32)) register_24 (.D(WRITE_DATA), .en(E30), .Q(R30), .clk(clock));  // open: clr
  Register #(.width(32)) register_25 (.D(WRITE_DATA), .en(E3), .Q(R3), .clk(clock));  // open: clr
  Register #(.width(32)) register_26 (.D(WRITE_DATA), .en(E7), .Q(R7), .clk(clock));  // open: clr
  Register #(.width(32)) register_27 (.D(WRITE_DATA), .en(E11), .Q(R11), .clk(clock));  // open: clr
  Register #(.width(32)) register_28 (.D(WRITE_DATA), .en(E15), .Q(R15), .clk(clock));  // open: clr
  Register #(.width(32)) register_29 (.D(WRITE_DATA), .en(E19), .Q(R19), .clk(clock));  // open: clr
  Register #(.width(32)) register_30 (.D(WRITE_DATA), .en(E23), .Q(R23), .clk(clock));  // open: clr
  Register #(.width(32)) register_31 (.D(WRITE_DATA), .en(E27), .Q(R27), .clk(clock));  // open: clr
  Register #(.width(32)) register_32 (.D(WRITE_DATA), .en(E31), .Q(R31), .clk(clock));  // open: clr
  Multiplexer #(.select(5), .width(32)) multiplexer_1 (
    .in0(R0), .in1(R1), .in2(R2), .in3(R3), .in4(R4), .in5(R5), .in6(R6), .in7(R7), .in8(R8), .in9(R9),
    .in10(R10), .in11(R11), .in12(R12), .in13(R13), .in14(R14), .in15(R15), .in16(R16), .in17(R17),
    .in18(R18), .in19(R19), .in20(R20), .in21(R21), .in22(R22), .in23(R23), .in24(R24), .in25(R25),
    .in26(R26), .in27(R27), .in28(R28), .in29(R29), .in30(R30), .in31(R31), .out(data2), .sel(RT));  // open: en
  Multiplexer #(.select(5), .width(32)) multiplexer_2 (
    .in0(R0), .in1(R1), .in2(R2), .in3(R3), .in4(R4), .in5(R5), .in6(R6), .in7(R7), .in8(R8), .in9(R9),
    .in10(R10), .in11(R11), .in12(R12), .in13(R13), .in14(R14), .in15(R15), .in16(R16), .in17(R17),
    .in18(R18), .in19(R19), .in20(R20), .in21(R21), .in22(R22), .in23(R23), .in24(R24), .in25(R25),
    .in26(R26), .in27(R27), .in28(R28), .in29(R29), .in30(R30), .in31(R31), .out(data1), .sel(RS));  // open: en
  // NOT_Gate not_1 has open pins: in=REG_WRTIE, out=open
  // NOT_Gate not_2 has open pins: in=REG_WRTIE, out=open

  // Other names for the same wires on the sheet: RW = REG_WRTIE; TU[31:0] = WRITE_DATA
endmodule

module ALU (
  input  CARRY_IN,
  input  [31:0] B,
  input  [31:0] A,
  input  [3:0] SELECT,
  output zero,
  output [31:0] R,
  output CARRY_OUT
);

  wire comparator_1_lt;
  wire [31:0] adder_1_out, and_1_out, bit_extender_1_out, or_1_out, subtractor_1_out;

  Subtractor #(.width(32)) subtractor_1 (.a(A), .b(B), .out(subtractor_1_out));  // open: bin, bout
  assign and_1_out = A & B;  // AND_Gate and_1, 32 bits wide
  assign or_1_out = A | B;  // OR_Gate or_1, 32 bits wide
  Adder #(.width(32)) adder_1 (.a(A), .b(B), .out(adder_1_out), .cin(CARRY_IN), .cout(CARRY_OUT));
  Comparator #(.width(32)) comparator_1 (.a(A), .b(B), .lt(comparator_1_lt));  // open: gt, eq
  assign bit_extender_1_out = {{31{1'b0}}, comparator_1_lt};  // Bit_Extender bit_extender_1
  Multiplexer #(.select(4), .width(32)) multiplexer_1 (
    .in0(and_1_out), .in1(or_1_out), .in2(adder_1_out), .in6(subtractor_1_out), .in7(bit_extender_1_out),
    .out(R), .sel(SELECT));  // open: in3, in4, in5, in8, in9, in10, in11, in12, in13, in14, in15, en
  Comparator #(.width(32)) comparator_2 (.a({32{1'b0}}), .b(R), .eq(zero));  // open: gt, lt
endmodule

module UC (
  input  OP5,
  input  OP4,
  input  OP3,
  input  OP2,
  input  OP1,
  input  OP0,
  output RegDst,
  output ALUSrc,
  output MemtoReg,
  output RegWrite,
  output MemRead,
  output MemWrite,
  output Branch,
  output ALUOp1,
  output ALUOp0,
  output Jump
);

  wire and_2_out, and_3_out, and_5_out, and_6_out, not_1_out, not_2_out, not_3_out, not_4_out, not_5_out,
       not_6_out, not_7_out, not_8_out, not_9_out, not_10_out, not_11_out, not_12_out, not_13_out,
       not_14_out, not_15_out, not_16_out, not_17_out, not_18_out, not_19_out, not_20_out, not_21_out,
       not_22_out, not_23_out, not_24_out, not_25_out, not_26_out, not_27_out, not_28_out, not_29_out,
       not_30_out, not_31_out, not_32_out, not_33_out, not_34_out, not_35_out, not_36_out, not_37_out,
       not_38_out, not_39_out, not_40_out, not_41_out, not_42_out, not_43_out, not_44_out, not_45_out,
       not_46_out, not_47_out, not_48_out, not_49_out, not_50_out;

  not not_1 (not_1_out, OP5);
  not not_2 (not_2_out, OP4);
  not not_3 (not_3_out, OP3);
  not not_4 (not_4_out, OP2);
  not not_5 (not_5_out, OP1);
  not not_6 (not_6_out, OP0);
  not not_7 (not_7_out, OP5);
  not not_8 (not_8_out, OP4);
  not not_9 (not_9_out, OP2);
  not not_10 (not_10_out, OP1);
  not not_11 (not_11_out, OP0);
  not not_12 (not_12_out, OP4);
  not not_13 (not_13_out, OP2);
  not not_14 (not_14_out, OP4);
  not not_15 (not_15_out, OP3);
  not not_16 (not_16_out, OP2);
  not not_17 (not_17_out, OP5);
  not not_18 (not_18_out, OP4);
  not not_19 (not_19_out, OP2);
  not not_20 (not_20_out, OP1);
  not not_21 (not_21_out, OP0);
  not not_22 (not_22_out, OP4);
  not not_23 (not_23_out, OP3);
  not not_24 (not_24_out, OP2);
  not not_25 (not_25_out, OP4);
  not not_26 (not_26_out, OP3);
  not not_27 (not_27_out, OP2);
  not not_28 (not_28_out, OP4);
  not not_29 (not_29_out, OP2);
  not not_30 (not_30_out, OP5);
  not not_31 (not_31_out, OP4);
  not not_32 (not_32_out, OP3);
  not not_33 (not_33_out, OP1);
  not not_34 (not_34_out, OP0);
  not not_35 (not_35_out, OP5);
  not not_36 (not_36_out, OP4);
  not not_37 (not_37_out, OP3);
  not not_38 (not_38_out, OP2);
  not not_39 (not_39_out, OP1);
  not not_40 (not_40_out, OP0);
  not not_41 (not_41_out, OP5);
  not not_42 (not_42_out, OP4);
  not not_43 (not_43_out, OP3);
  not not_44 (not_44_out, OP1);
  not not_45 (not_45_out, OP0);
  not not_46 (not_46_out, OP5);
  not not_47 (not_47_out, OP4);
  not not_48 (not_48_out, OP3);
  not not_49 (not_49_out, OP2);
  not not_50 (not_50_out, OP0);
  and and_1 (RegDst, not_1_out, not_2_out, not_3_out, not_4_out, not_5_out, not_6_out);
  and and_2 (and_2_out, not_7_out, not_8_out, OP3, not_9_out, not_10_out, not_11_out);
  and and_3 (and_3_out, OP5, not_12_out, not_13_out, OP1, OP0);
  and and_4 (MemtoReg, OP5, not_14_out, not_15_out, not_16_out, OP1, OP0);
  and and_5 (and_5_out, not_17_out, not_18_out, not_19_out, not_20_out, not_21_out);
  and and_6 (and_6_out, OP5, not_22_out, not_23_out, not_24_out, OP1, OP0);
  and and_7 (MemRead, OP5, not_25_out, not_26_out, not_27_out, OP1, OP0);
  and and_8 (MemWrite, OP5, not_28_out, OP3, not_29_out, OP1, OP0);
  and and_9 (Branch, not_30_out, not_31_out, not_32_out, OP2, not_33_out, not_34_out);
  and and_10 (ALUOp1, not_35_out, not_36_out, not_37_out, not_38_out, not_39_out, not_40_out);
  and and_11 (ALUOp0, not_41_out, not_42_out, not_43_out, OP2, not_44_out, not_45_out);
  and and_12 (Jump, not_46_out, not_47_out, not_48_out, not_49_out, OP1, not_50_out);
  or or_1 (ALUSrc, and_2_out, and_3_out);
  or or_2 (RegWrite, and_5_out, and_6_out);
endmodule

module ALU_UC (
  input  ALUOp1,
  input  ALUOp0,
  input  F5,
  input  F4,
  input  F3,
  input  F2,
  input  F1,
  input  F0,
  output O3,
  output O2,
  output O1,
  output O0
);

  wire and_1_out, and_2_out, and_3_out, and_4_out, not_1_out, not_2_out, not_3_out;

  not not_1 (not_1_out, ALUOp1);
  and and_1 (and_1_out, not_1_out, ALUOp0);
  and and_2 (and_2_out, ALUOp1, F1);
  not not_2 (not_2_out, ALUOp1);
  or or_1 (O1, not_2_out, not_3_out);
  not not_3 (not_3_out, F2);
  and and_3 (and_3_out, ALUOp1, F0);
  and and_4 (and_4_out, ALUOp1, F3);
  or or_2 (O2, and_1_out, and_2_out);
  or or_3 (O0, and_3_out, and_4_out);

  assign O3 = 1'b0;
endmodule
